// Logisim project my_xor.circ as structural Verilog: 3 circuits, main circuit main
module main (
  input  X,
  input  Y,
  output X_XOR_Y
);

  wire and_1_out, and_2_out, not_1_out, not_2_out;

  not not_1 (not_1_out, X);
  not not_2 (not_2_out, Y);
  and and_1 (and_1_out, not_1_out, Y);
  and and_2 (and_2_out, X, not_2_out);
  or or_1 (X_XOR_Y, and_1_out, and_2_out);
endmodule

module onebit_adder (
  input  A,
  input  B,
  input  Cin,
  output S,
  output Cout
);

  wire and_1_out, and_2_out, and_3_out, and_4_out, and_5_out, and_6_out, and_7_out, not_1_out, not_2_out,
       not_3_out;

  not not_1 (not_1_out, A);
  not not_2 (not_2_out, B);
  not not_3 (not_3_out, Cin);
  and and_1 (and_1_out, not_1_out, not_2_out, Cin);
  and and_2 (and_2_out, not_1_out, B, not_3_out);
  and and_3 (and_3_out, A, not_2_out, not_3_out);
  and and_4 (and_4_out, A, B, Cin);
  and and_5 (and_5_out, B, Cin);
  and and_6 (and_6_out, A, Cin);
  and and_7 (and_7_out, A, B);
  or or_1 (S, and_1_out, and_2_out, and_3_out, and_4_out);
  or or_2 (Cout, and_5_out, and_6_out, and_7_out);
endmodule

module twobit_adder (
  input  [1:0] A,
  input  [1:0] B,
  input  in_3,
  output [1:0] out_4,
  output Cout
);

  wire onebit_adder_2_cout;

  onebit_adder onebit_adder_1 (.A(B[0]), .B(B[1]), .Cin(onebit_adder_2_cout), .S(out_4[1]), .Cout(Cout));
  onebit_adder onebit_adder_2 (.A(A[0]), .B(A[1]), .Cin(in_3), .S(out_4[0]), .Cout(onebit_adder_2_cout));
endmodule
